# Fritzing sketch layout (saved by Fritzing 0.9.3b)
breadboards: 1

parts:
  Part1 = Arduino Uno (Rev3)
  U2 = LCD-16X2 [package=lcd-16x2]
  U3 = POT [package=pot_mammoth]
  U4 = POT [package=pot_mammoth]
  J1 = Piezo Speaker

nets:
  N1: Part1.A2, U3.A
  N2: Part1.D8, U2.E
  N3: Part1.D9_PWM, U2.DB4
  N4: Part1.D10_PWM/SS, U2.DB5
  N5: Part1.D11_PWM/MOSI, U2.DB6
  N6: Part1.D12/MISO, U2.DB7
  N7: Part1.D3_PWM, J1.pin2
  N8: Part1.D7, U2.RS
  5V: Part1.5V, U2.VDD, U2.A, U3.E, U4.S
  GND: Part1.GND, U2.VSS, U2.K, U3.S, U4.E, J1.pin1
  N9: U2.VO, U4.A
